// Logisim project ex4.circ as structural Verilog: 5 circuits, main circuit RotRight
module RotRight (
  input  [15:0] INPUT0,
  input  [3:0] AMOUNT,
  output [15:0] OUTPUT0
);

  Multiplexer #(.enable("false"), .select(4)) multiplexer_1 (
    .in0(INPUT0[0]), .in1(INPUT0[1]), .in2(INPUT0[2]), .in3(INPUT0[3]), .in4(INPUT0[4]), .in5(INPUT0[5]),
    .in6(INPUT0[6]), .in7(INPUT0[7]), .in8(INPUT0[8]), .in9(INPUT0[9]), .in10(INPUT0[10]), .in11(INPUT0[11]),
    .in12(INPUT0[12]), .in13(INPUT0[13]), .in14(INPUT0[14]), .in15(INPUT0[15]), .sel(AMOUNT));  // open: out
endmodule

module rot1 (
  input  [15:0] in_1,
  output [15:0] out_2
);


  assign out_2 = {in_1[0], in_1[15:1]};
endmodule

module rot2 (
  input  [15:0] in_1,
  output [15:0] out_2
);


  assign out_2 = {in_1[1:0], in_1[15:2]};
endmodule

module rot4 (
  input  [15:0] in_1,
  output [15:0] out_2
);


  assign out_2 = {in_1[3:0], in_1[15:4]};
endmodule

module rot8 (
  input  [15:0] in_1,
  output [15:0] out_2
);


  assign out_2 = {in_1[7:0], in_1[15:8]};
endmodule
